// Logisim project PC logic.circ as structural Verilog: 1 circuit, main circuit main
module main (
  input  [7:0] Ra,
  input  in_2,
  input  in_3,
  input  in_4,
  input  in_5,
  input  in_6,
  input  Reset,
  input  in_8
);

  wire and_1_out, clock_1_out, not_1_out, not_2_out;
  wire [2:0] ram_1_data_2;
  wire [4:0] ram_1_data;
  wire [7:0] adder_1_out, multiplexer_1_out, multiplexer_2_out, PC_q;

  Multiplexer #(.width(8)) multiplexer_1 (.in0(Ra), .in1(adder_1_out), .out(multiplexer_1_out), .sel(in_2), .en(in_3));
  Clock clock_1 (.out(clock_1_out));
  Register PC (.D(multiplexer_1_out), .en(in_3), .Q(PC_q), .clk(clock_1_out), .clr(Reset));
  Multiplexer #(.width(8)) multiplexer_2 (
    .in0(8'h1), .in1({{5{in_6}}, ram_1_data_2}), .out(multiplexer_2_out), .sel(and_1_out), .en(in_5));
  Adder adder_1 (.a(multiplexer_2_out), .b(PC_q), .out(adder_1_out), .cin(in_4));  // open: cout
  and and_1 (and_1_out, not_1_out, ram_1_data[1], not_2_out);
  not not_1 (not_1_out, ram_1_data[0]);
  not not_2 (not_2_out, ram_1_data[2]);
  RAM ram_1 (.addr(PC_q), .data({ram_1_data_2, ram_1_data}), .clk(clock_1_out), .ld(in_8));  // open: sel, clr
endmodule
