// Logisim project PRESHIT.circ as structural Verilog: 12 circuits, main circuit PC counter
module ALU (
  input  [7:0] A,
  input  ALU_enable,
  input  [2:0] control_signal,
  input  [7:0] B,
  output [7:0] ALU_Output,
  output Carry_bit
);

  wire ADDER_c, SUB_c;
  wire [7:0] ADDER_a___b, AND_a_b, multiplier_1_out, OR_a__b, SUB_a___b, XOR_a___b;

  AND AND (.A(A), .B(B), .A_B(AND_a_b));
  OR OR (.A(A), .B(B), .A__B(OR_a__b));
  XOR XOR (.A(A), .B(B), .A___B(XOR_a___b));
  ADDER ADDER (.Cin(1'b0), .a(A), .b(B), .a___b(ADDER_a___b), .c(ADDER_c));
  SUB SUB (.a(A), .B(B), .A___B(SUB_a___b), .C(SUB_c));
  Multiplier multiplier_1 (.a(A), .b(B), .out(multiplier_1_out));  // open: cin, cout
  Multiplexer #(.select(3), .width(8)) multiplexer_1 (
    .in0(AND_a_b), .in1(OR_a__b), .in2(XOR_a___b), .in3(ADDER_a___b), .in4(SUB_a___b),
    .in5(multiplier_1_out), .in6(A), .in7(B), .out(ALU_Output), .sel(control_signal), .en(ALU_enable));
  Multiplexer #(.select(3)) multiplexer_2 (
    .in0(1'b0), .in1(1'b0), .in2(1'b0), .in3(ADDER_c), .in4(SUB_c), .in5(1'b0), .in6(1'b0), .in7(1'b0),
    .out(Carry_bit), .sel(control_signal), .en(ALU_enable));

  // Notes on the sheet:
  //   ALU
endmodule

module AND (
  input  [7:0] A,
  input  [7:0] B,
  output [7:0] A_B
);

  assign A_B = A & B;  // AND_Gate and_1, 8 bits wide
endmodule

module OR (
  input  [7:0] A,
  input  [7:0] B,
  output [7:0] A__B
);

  assign A__B = A | B;  // OR_Gate or_1, 8 bits wide
endmodule

module XOR (
  input  [7:0] A,
  input  [7:0] B,
  output [7:0] A___B
);

  assign A___B = A ^ B;  // XOR_Gate xor_1, 8 bits wide
endmodule

module ADDER (
  input  Cin,
  input  [7:0] a,
  input  [7:0] b,
  output [7:0] a___b,
  output c
);

  wire FA_2_cout, FA_3_cout, FA_4_cout, FA_5_cout, FA_6_cout, FA_7_cout, FA_cout;

  FA FA (.Cin(a[0]), .A(b[0]), .B(Cin), .SUM1(a___b[0]), .COUT(FA_cout));
  FA FA_2 (.Cin(a[1]), .A(b[1]), .B(FA_cout), .SUM1(a___b[1]), .COUT(FA_2_cout));
  FA FA_3 (.Cin(a[2]), .A(b[2]), .B(FA_2_cout), .SUM1(a___b[2]), .COUT(FA_3_cout));
  FA FA_4 (.Cin(a[3]), .A(b[3]), .B(FA_3_cout), .SUM1(a___b[3]), .COUT(FA_4_cout));
  FA FA_5 (.Cin(a[4]), .A(b[4]), .B(FA_4_cout), .SUM1(a___b[4]), .COUT(FA_5_cout));
  FA FA_6 (.Cin(a[5]), .A(b[5]), .B(FA_5_cout), .SUM1(a___b[5]), .COUT(FA_6_cout));
  FA FA_7 (.Cin(a[6]), .A(b[6]), .B(FA_6_cout), .SUM1(a___b[6]), .COUT(FA_7_cout));
  FA FA_8 (.Cin(a[7]), .A(b[7]), .B(FA_7_cout), .SUM1(a___b[7]), .COUT(c));
endmodule

module FA (
  input  Cin,
  input  A,
  input  B,
  output SUM1,
  output COUT
);

  wire and_1_out, and_2_out, xor_1_out;

  xor xor_1 (xor_1_out, A, B);
  and and_1 (and_1_out, A, B);
  xor xor_2 (SUM1, Cin, xor_1_out);
  and and_2 (and_2_out, xor_1_out, Cin);
  or or_1 (COUT, and_2_out, and_1_out);
endmodule

module SUB (
  input  [7:0] a,
  input  [7:0] B,
  output [7:0] A___B,
  output C
);

  wire [7:0] adder_a___b, xor_a___b;

  XOR \xor  (.A(B), .B({8{1'b1}}), .A___B(xor_a___b));
  ADDER adder (.Cin(1'b0), .a(a), .b(xor_a___b), .a___b(adder_a___b));  // open: c
  ADDER adder_2 (.Cin(1'b0), .a(adder_a___b), .b(8'h1), .a___b(A___B), .c(C));
endmodule

module Register_file (
  input  clock,
  input  write_signal,
  input  [1:0] A_addrs,
  input  read_enab,
  input  wrt_enab,
  input  [1:0] wrt_addrs,
  input  [1:0] B_addrs,
  input  RESET,
  input  [7:0] input_data,
  output [7:0] A,
  output [7:0] B
);

  wire and_1_out, and_2_out, and_3_out, and_4_out, decoder_1_out0, decoder_1_out1, decoder_1_out2,
       decoder_1_out3;
  wire [7:0] register_1_q, register_2_q, register_3_q, register_4_q;

  Decoder #(.select(2)) decoder_1 (
    .out0(decoder_1_out0), .out1(decoder_1_out1), .out2(decoder_1_out2), .out3(decoder_1_out3),
    .sel(wrt_addrs), .en(wrt_enab));
  and and_1 (and_1_out, decoder_1_out0, write_signal);
  and and_2 (and_2_out, write_signal, decoder_1_out1);
  and and_3 (and_3_out, write_signal, decoder_1_out2);
  and and_4 (and_4_out, write_signal, decoder_1_out3);
  Register register_1 (.D(input_data), .en(and_1_out), .Q(register_1_q), .clk(clock), .clr(RESET));
  Register register_2 (.D(input_data), .en(and_2_out), .Q(register_2_q), .clk(clock), .clr(RESET));
  Register register_3 (.D(input_data), .en(and_3_out), .Q(register_3_q), .clk(clock), .clr(RESET));
  Register register_4 (.D(input_data), .en(and_4_out), .Q(register_4_q), .clk(clock), .clr(RESET));
  Multiplexer #(.select(2), .width(8)) multiplexer_1 (
    .in0(register_1_q), .in1(register_2_q), .in2(register_3_q), .in3(register_4_q), .out(A), .sel(A_addrs));  // open: en
  Multiplexer #(.select(2), .width(8)) multiplexer_2 (
    .in0(register_1_q), .in1(register_2_q), .in2(register_3_q), .in3(register_4_q), .out(B), .sel(B_addrs));  // open: en
endmodule

module PC_counter (
  input  Reset,
  input  in_2,
  output Carry_bit,
  output [2:0] out_4,
  output [1:0] out_5,
  output [1:0] out_6
);

  wire _0, _1, _2, _3, _4, and_1_out, and_2_out, and_3_out, and_4_out, and_5_out, and_6_out, and_7_out,
       and_8_out, and_9_out, and_10_out, and_11_out, and_12_out, and_13_out, and_14_out, and_15_out,
       and_16_out, B_SEL, HLT, jm, JMP, main_c, MEM_WRT, not_1_out, not_2_out, or_1_out, or_2_out, or_3_out,
       WRT_SIG, Y_SEL;
  wire [1:0] AD_C;
  wire [2:0] counter_5_q;
  wire [3:0] IR_q, IR_q_2;
  wire [7:0] adder_1_out, adder_3_out, ADDR, alu_1_alu_output, DATA, \do , IV, multiplexer_1_out,
       multiplexer_2_out, multiplexer_5_out, multiplexer_6_out, multiplexer_7_out, multiplexer_8_out, PC, Ra,
       Rb_q, register_1_q, register_file_1_a, register_file_1_b, Rm_q, Ry_q, Rz_q, subtractor_1_out;

  and and_1 (and_1_out, main_c, _4);
  Register_file register_file_1 (
    .clock(and_1_out), .write_signal(WRT_SIG), .wrt_enab(_4), .wrt_addrs(AD_C), .RESET(Reset),
    .input_data(Ry_q), .A(register_file_1_a), .A_addrs(out_6), .read_enab(_1), .B(register_file_1_b),
    .B_addrs(out_5));
  Register Rb (.D(register_file_1_b), .Q(Rb_q), .clk(and_2_out), .clr(Reset));  // open: en
  Multiplexer #(.width(8)) multiplexer_1 (.in0(Rb_q), .in1(IV), .out(multiplexer_1_out), .sel(B_SEL), .en(_2));
  Register u_Ra (.D(register_file_1_a), .Q(Ra), .clk(and_2_out), .clr(Reset));  // open: en
  and and_2 (and_2_out, _1, main_c);
  ALU alu_1 (
    .A(Ra), .B(multiplexer_1_out), .ALU_Output(alu_1_alu_output), .ALU_enable(_2), .control_signal(out_4),
    .Carry_bit(Carry_bit));
  and and_3 (and_3_out, main_c, _2);
  Register Rz (.D(alu_1_alu_output), .Q(Rz_q), .clk(and_3_out), .clr(Reset));  // open: en
  Multiplexer #(.width(8)) multiplexer_2 (.in0(Rz_q), .in1(DATA), .out(multiplexer_2_out), .sel(Y_SEL));  // open: en
  and and_4 (and_4_out, main_c, _2);
  Register Ry (.D(multiplexer_2_out), .Q(Ry_q), .clk(and_5_out), .clr(Reset));  // open: en
  and and_5 (and_5_out, main_c, _3);
  Clock main_counter (.out(main_c));
  Register Rm (.D(Rb_q), .Q(Rm_q), .clk(and_4_out), .clr(Reset));  // open: en
  Multiplexer #(.width(8)) multiplexer_3 (.in0(Rm_q), .out(DATA), .sel(1'b0), .en(and_7_out));  // open: in1
  Multiplexer #(.width(8)) multiplexer_4 (.in0(Rz_q), .out(ADDR), .sel(1'b0), .en(and_6_out));  // open: in1
  and and_6 (and_6_out, _3, or_1_out);
  and and_7 (and_7_out, MEM_WRT, _3);
  or or_1 (or_1_out, Y_SEL, MEM_WRT);
  Adder adder_1 (.a(\do ), .b(8'h1), .out(adder_1_out));  // open: cin, cout
  and and_8 (and_8_out, main_c, _0);
  and and_9 (and_9_out, main_c, B_SEL, _2);
  Register IR (.D(DATA), .Q({IR_q_2, IR_q}), .clk(and_10_out), .clr(Reset));  // open: en
  and and_10 (and_10_out, main_c, _0);
  and and_11 (and_11_out, JMP, _3);
  Multiplexer #(.width(8)) multiplexer_5 (.in0(adder_3_out), .in1(IV), .out(multiplexer_5_out), .sel(JMP));  // open: en
  Multiplexer #(.width(8)) multiplexer_6 (
    .in0(multiplexer_5_out), .in1(adder_1_out), .out(multiplexer_6_out), .sel(jm));  // open: en
  or or_2 (or_2_out, and_8_out, and_9_out);
  Counter #(.width(3), .max('h4), .trigger("falling")) counter_5 (
    .Q(counter_5_q), .clk(main_c), .clr(Reset));  // open: load, D, count, carry
  Register register_1 (.D(IV), .Q(register_1_q), .clk(and_11_out));  // open: en, clr
  Register u_PC (.D(multiplexer_6_out), .Q(PC), .clk(or_2_out), .clr(Reset));  // open: en
  Subtractor subtractor_1 (.a(PC), .b(8'h1), .out(subtractor_1_out));  // open: bin, bout
  if_counter if_counter_1 (.in_1(counter_5_q), ._0(_0), ._1(_1), ._2(_2), ._3(_3), ._4(_4));
  Adder adder_2 (.a(register_1_q), .b(8'h1), .out(\do ));  // open: cin, cout
  or or_3 (or_3_out, JMP, HLT);
  Multiplexer #(.width(8)) multiplexer_7 (
    .in0(8'h1), .in1({8{1'b0}}), .out(multiplexer_7_out), .sel(or_3_out));  // open: en
  signals signals_1 (
    .DATAS(IR_q), .OPCODE(IR_q_2), .MEM_WRT(MEM_WRT), .ALU_SEL(out_4), .Rb(out_5), .Ra(out_6), .ADDR_C(AD_C),
    .HLT(HLT), .WRT_SIG(WRT_SIG), .B_SEL(B_SEL), .JMP_C(JMP), .YSEL(Y_SEL));
  Register #(.width(1)) register_2 (.D(JMP), .Q(jm), .clk(and_12_out));  // open: en, clr
  and and_12 (and_12_out, _4, main_c);
  Multiplexer #(.width(8)) multiplexer_8 (
    .in0(ADDR), .in1(subtractor_1_out), .out(multiplexer_8_out), .sel(HLT));  // open: en
  Multiplexer #(.width(8)) multiplexer_9 (.in0(PC), .in1(\do ), .out(ADDR), .sel(jm), .en(and_13_out));
  and and_13 (and_13_out, IR_q_2[3], _1);
  Adder adder_3 (.a(multiplexer_7_out), .b(PC), .out(adder_3_out), .cin(in_2));  // open: cout
  Multiplexer #(.width(8)) multiplexer_10 (.in0(PC), .out(ADDR), .sel(1'b0), .en(and_14_out));  // open: in1
  and and_14 (and_14_out, _0, not_1_out);
  not not_1 (not_1_out, HLT);
  RAM ram_1 (.addr(multiplexer_8_out), .data(DATA), .clk(main_c), .ld(not_2_out));  // open: sel, clr
  not not_2 (not_2_out, and_15_out);
  and and_15 (and_15_out, MEM_WRT, _3);
  Register register_3 (.D(DATA), .Q(IV), .clk(and_16_out), .clr(Reset));  // open: en
  and and_16 (and_16_out, main_c, _1);

  // Other names for the same wires on the sheet: ALU_SEL[2:0] = out_4; main_re = Reset; Ra_AD[1:0] = out_6;
  //   Rb_AD[1:0] = out_5
endmodule

module if_counter (
  input  [2:0] in_1,
  output _0,
  output _1,
  output _2,
  output _3,
  output _4
);

  wire not_1_out, not_2_out, not_3_out, not_4_out, not_5_out, not_6_out, not_7_out, not_8_out, not_9_out,
       not_10_out;

  not not_1 (not_1_out, in_1[2]);
  not not_2 (not_2_out, in_1[0]);
  not not_3 (not_3_out, in_1[1]);
  and and_1 (_0, not_1_out, not_3_out, not_2_out);
  not not_4 (not_4_out, in_1[2]);
  not not_5 (not_5_out, in_1[1]);
  and and_2 (_1, not_4_out, not_5_out, in_1[0]);
  not not_6 (not_6_out, in_1[2]);
  and and_3 (_2, not_6_out, in_1[1], not_7_out);
  not not_7 (not_7_out, in_1[0]);
  not not_8 (not_8_out, in_1[2]);
  and and_4 (_3, not_8_out, in_1[1], in_1[0]);
  not not_9 (not_9_out, in_1[1]);
  not not_10 (not_10_out, in_1[0]);
  and and_5 (_4, in_1[2], not_9_out, not_10_out);

  // Other names for the same wires on the sheet: LSB = in_1[0]; MID = in_1[1]; MSB = in_1[2]
endmodule

module DECODE (
  input  [3:0] OP_CODE,
  output ADD,
  output MOV,
  output SUBT,
  output HLT,
  output MULT,
  output STA,
  output AND,
  output JMP,
  output OR,
  output LAD,
  output XOR
);

  wire not_1_out, not_2_out, not_3_out, not_4_out, not_5_out, not_6_out, not_7_out, not_8_out, not_9_out,
       not_10_out, not_11_out, not_12_out, not_13_out, not_14_out, not_15_out, not_16_out, not_17_out,
       not_18_out, not_19_out, not_20_out, not_21_out, not_22_out, not_23_out, not_24_out, not_25_out,
       not_26_out, not_27_out;

  not not_1 (not_1_out, OP_CODE[0]);
  not not_2 (not_2_out, OP_CODE[1]);
  not not_3 (not_3_out, OP_CODE[2]);
  not not_4 (not_4_out, OP_CODE[3]);
  not not_5 (not_5_out, OP_CODE[1]);
  not not_6 (not_6_out, OP_CODE[2]);
  not not_7 (not_7_out, OP_CODE[3]);
  not not_8 (not_8_out, OP_CODE[0]);
  not not_9 (not_9_out, OP_CODE[2]);
  not not_10 (not_10_out, OP_CODE[3]);
  not not_11 (not_11_out, OP_CODE[3]);
  not not_12 (not_12_out, OP_CODE[0]);
  not not_13 (not_13_out, OP_CODE[1]);
  not not_14 (not_14_out, OP_CODE[3]);
  not not_15 (not_15_out, OP_CODE[1]);
  not not_16 (not_16_out, OP_CODE[3]);
  not not_17 (not_17_out, OP_CODE[2]);
  and and_1 (ADD, not_1_out, not_2_out, not_3_out, not_4_out);
  and and_2 (SUBT, OP_CODE[0], not_5_out, not_6_out, not_7_out);
  and and_3 (MULT, not_8_out, OP_CODE[1], not_9_out, not_10_out);
  and and_4 (AND, OP_CODE[0], OP_CODE[1], not_17_out, not_11_out);
  and and_5 (OR, not_12_out, not_13_out, OP_CODE[2], not_14_out);
  and and_6 (XOR, OP_CODE[0], not_15_out, OP_CODE[2], not_16_out);
  not not_18 (not_18_out, OP_CODE[0]);
  not not_19 (not_19_out, OP_CODE[3]);
  not not_20 (not_20_out, OP_CODE[3]);
  not not_21 (not_21_out, OP_CODE[0]);
  not not_22 (not_22_out, OP_CODE[1]);
  not not_23 (not_23_out, OP_CODE[2]);
  not not_24 (not_24_out, OP_CODE[1]);
  not not_25 (not_25_out, OP_CODE[2]);
  not not_26 (not_26_out, OP_CODE[0]);
  not not_27 (not_27_out, OP_CODE[2]);
  and and_7 (MOV, not_18_out, OP_CODE[1], OP_CODE[2], not_19_out);
  and and_8 (HLT, OP_CODE[0], OP_CODE[1], OP_CODE[2], not_20_out);
  and and_9 (STA, not_21_out, not_22_out, not_23_out, OP_CODE[3]);
  and and_10 (JMP, OP_CODE[0], not_24_out, not_25_out, OP_CODE[3]);
  and and_11 (LAD, not_26_out, OP_CODE[1], not_27_out, OP_CODE[3]);

  // Other names for the same wires on the sheet: _0_B = OP_CODE[0]; _1_B = OP_CODE[1]; _2_B = OP_CODE[2];
  //   _3_B = OP_CODE[3]
endmodule

module signals (
  input  [3:0] DATAS,
  input  [3:0] OPCODE,
  output MEM_WRT,
  output [2:0] ALU_SEL,
  output [1:0] Rb,
  output [1:0] Ra,
  output [1:0] ADDR_C,
  output HLT,
  output WRT_SIG,
  output B_SEL,
  output JMP_C,
  output YSEL
);

  wire ADD, AND, MOV, MULT, OR, or_1_out, or_3_out, SUBT, XOR;

  DECODE decode_1 (
    .OP_CODE(OPCODE), .ADD(ADD), .MOV(MOV), .SUBT(SUBT), .HLT(HLT), .MULT(MULT), .STA(MEM_WRT), .AND(AND),
    .JMP(JMP_C), .OR(OR), .LAD(YSEL), .XOR(XOR));
  not not_1 (WRT_SIG, or_1_out);
  or or_1 (or_1_out, HLT, MEM_WRT, JMP_C);
  or or_2 (B_SEL, MEM_WRT, JMP_C, YSEL);
  Multiplexer #(.width(3)) multiplexer_1 (.in0(3'b000), .out(ALU_SEL), .sel(1'b0), .en(AND));  // open: in1
  Multiplexer #(.width(3)) multiplexer_2 (.in0(3'b001), .out(ALU_SEL), .sel(1'b0), .en(OR));  // open: in1
  Multiplexer #(.width(3)) multiplexer_3 (.in0(3'b010), .out(ALU_SEL), .sel(1'b0), .en(XOR));  // open: in1
  Multiplexer #(.width(3)) multiplexer_4 (.in0(3'b011), .out(ALU_SEL), .sel(1'b0), .en(ADD));  // open: in1
  Multiplexer #(.width(3)) multiplexer_5 (.in0(3'b100), .out(ALU_SEL), .sel(1'b0), .en(SUBT));  // open: in1
  Multiplexer #(.width(3)) multiplexer_6 (.in0(3'b101), .out(ALU_SEL), .sel(1'b0), .en(MULT));  // open: in1
  Multiplexer #(.width(3)) multiplexer_7 (.in0(3'b110), .out(ALU_SEL), .sel(1'b0), .en(1'b0));  // open: in1
  Multiplexer #(.width(3)) multiplexer_8 (.in0(3'b111), .out(ALU_SEL), .sel(1'b0), .en(or_3_out));  // open: in1
  or or_3 (or_3_out, YSEL, MOV, JMP_C, MEM_WRT);

  assign ADDR_C = DATAS[3:2];
  assign Ra = DATAS[3:2];
  assign Rb = DATAS[1:0];

  // Other names for the same wires on the sheet: JMP = JMP_C; LAD = YSEL; STA = MEM_WRT
endmodule
